// Digital circuit comp_screen.dig as structural Verilog
module comp_screen (
  input  clk
);

  wire and_2_out, and_3_out, nna8v0_1_p4, not_1_out, not_2_out, onvram, rw;
  wire [3:0] counter_1_out;
  wire [7:0] abus, dbus, vram_d1, vram_d2;

  Counter #(.Bits(4)) counter_1 (.en(1'b1), .C(clk), .clr(1'b0), .out(counter_1_out));  // open: ovf
  // nna8v0 nna8v0_1: pin names not known; wires that end beside it: clk, abus, dbus, nna8v0_1_p4, rw, nna8v0_1_p4
  and and_1 (onvram, abus[4], abus[5], abus[6], abus[7]);
  not not_1 (not_1_out, rw);
  RAMDualAccess #(.AddrBits(4), .Bits(8)) vram (
    .str(rw), .C(clk), .ld(not_1_out), .A1(abus[3:0]), .Din1(dbus), .A2(counter_1_out), .D1(vram_d1),
    .D2(vram_d2));
  and and_2 (and_2_out, ~onvram, ~clk);  // And
  and and_3 (and_3_out, clk, rw);
  not not_2 (not_2_out, onvram);
  TransGate #(.Bits(8)) transgate_1 (.A(onvram), .nA(not_2_out), .out1(vram_d1), .out2(dbus));
  EEPROM #(.AddrBits(8), .isProgramMemory("true"), .Bits(8)) eeprom_1 (
    .A(abus), .CS(and_2_out), .WE(and_3_out), .OE(~rw), .D(dbus));
  LedMatrix #(.colAddrBits(4), .ledPersistence("true")) ledmatrix_1 (.rows(vram_d2), .column(counter_1_out));

  // Other names for the same wires on the sheet: C = clk

  // Notes on the sheet:
  //   clk: Hz: 2147483647
  //   video
  //   cpu
  //   main mem
  //   contents of eeprom_1 (hex, n*v repeats v):
  //   22,58,4c,e,20,1e,33,3e,23,10,54,24,10,1,4,17*0,20,e,14*0,48,65
  //   ,6c,6c,6f,20,57,6f,72,6c,64,21,21,0,0,0,10,2f,58,4d,f0,83,6c,c
  //   ,3e,a,6,63,22,10,4c,47,f,33,5,157*0,48,65,6c,6c,6f,20,57,6f,72
  //   ,6c,64,21,21
endmodule
