// Digital circuit nna1.dig as structural Verilog
module nna1 (
  input  clk,
  output [7:0] out_1,
  output [7:0] out_2,
  output [7:0] out_3,
  output [7:0] out_4
);

  wire add, add_1_c_o, add_2_c_o, \and , and_1_out, and_3_out, and_4_out, and_5_out, and_6_out, and_9_out,
       and_10_out, and_11_out, and_12_out, and_13_out, and_14_out, and_16_out, and_17_out, and_21_out,
       and_24_out, and_25_out, and_26_out, and_27_out, and_28_out, and_29_out, bra, c_prog, clf,
       comparator_1_eq, comparator_1_lt, dec, decoder_1_out_0, decoder_1_out_1, decoder_1_out_2,
       decoder_1_out_3, decoder_2_out_0, decoder_3_out_0, decoder_3_out_1, decoder_3_out_2, decoder_3_out_3,
       eq, exec_2_nq, exec_2_q, flf, gt, inc, jmp, lih, lil, mov, mrd, mul, mwr, \nand , not_1_out,
       not_2_out, not_3_out, not_4_out, not_5_out, not_6_out, not_7_out, not_8_out, not_9_out, not_10_out,
       not_11_out, not_12_out, not_13_out, not_14_out, not_15_out, oflag_out, \or , or_1_out, or_2_out,
       or_3_out, or_4_out, or_5_out, or_7_out, or_8_out, rol, sub_1_c_o, t_ff_1_q, \xor ;
  wire [1:0] and_7_out;
  wire [3:0] arg;
  wire [7:0] add_1_s, add_2_s, and_23_out, barrelshifter_1_out, barrelshifter_2_out, mul_1_mul, nand_1_out,
       or_6_out, PC_out, regin, regout_arg0, regout_arg1, sub_1_s, xor_1_out;
  wire [7:4] rom_1_d;

  T_FF t_ff_1 (.T(1'b1), .C(clk), .Q(t_ff_1_q));  // open: nQ
  and and_1 (and_1_out, clk, exec_2_nq);
  or or_1 (or_1_out, c_prog, and_1_out);
  and and_2 (c_prog, t_ff_1_q, exec_2_q);
  LED exec (.in(exec_2_q));
  CounterPreset #(.Bits(8)) PC (
    .en(1'b1), .C(or_1_out), .dir(1'b0), .in({8{1'b0}}), .ld(1'b0), .clr(and_4_out), .out(PC_out));  // open: ovf
  Break prog_load_done (.brk(and_4_out));
  not not_1 (not_1_out, and_4_out);
  and and_3 (and_3_out, PC_out[0], PC_out[1], PC_out[2], PC_out[3]);
  and and_4 (and_4_out, exec_2_nq, and_3_out);
  RS_FF_AS exec_2 (.S(and_5_out), .R(1'b0), .Q(exec_2_q), .nQ(exec_2_nq));
  and and_5 (and_5_out, ~t_ff_1_q, and_3_out);  // And
  and and_6 (and_6_out, not_1_out, exec_2_nq);
  ROM #(.AddrBits(8), .Bits(8)) rom_1 (.A(PC_out), .sel(exec_2_nq), .D({rom_1_d, arg}));
  or or_2 (or_2_out, and_6_out, 1'b0);
  RAMSinglePortSel #(.AddrBits(8), .isProgramMemory("true"), .Bits(8)) main_mem (
    .A(PC_out), .CS(1'b1), .WE(or_2_out), .OE(1'b1), .D({rom_1_d, arg}));
  or or_3 (or_3_out, lil, lih);
  or or_4 (or_4_out, mul, \nand , \and , \or , \xor );
  and and_7 (and_7_out[1], arg[3], ~or_3_out);  // And
  and and_8 (and_7_out[0], arg[2], ~or_3_out);  // And
  or or_5 (or_5_out, inc, dec, mov, add, lil, lih, rol, or_4_out);
  Decoder #(.Selector_Bits(2)) decoder_1 (
    .sel(and_7_out), .out_0(decoder_1_out_0), .out_1(decoder_1_out_1), .out_2(decoder_1_out_2),
    .out_3(decoder_1_out_3));
  Decoder #(.Selector_Bits(4)) decoder_2 (
    .sel(rom_1_d), .out_0(decoder_2_out_0), .out_1(lil), .out_2(lih), .out_3(mwr), .out_4(mrd), .out_5(mov),
    .out_6(bra), .out_7(rol), .out_8(eq), .out_9(gt), .out_10(add), .out_11(mul), .out_12(\and ),
    .out_13(\nand ), .out_14(\or ), .out_15(\xor ));
  and and_9 (and_9_out, or_5_out, decoder_1_out_0);
  and and_10 (and_10_out, or_5_out, decoder_1_out_1);
  and and_11 (and_11_out, or_5_out, decoder_1_out_2);
  and and_12 (and_12_out, or_5_out, decoder_1_out_3);
  Decoder #(.Selector_Bits(2)) decoder_3 (
    .sel(arg[1:0]), .out_0(decoder_3_out_0), .out_1(decoder_3_out_1), .out_2(decoder_3_out_2),
    .out_3(decoder_3_out_3));
  and and_13 (and_13_out, ~arg[2], ~arg[3]);  // And
  and and_14 (and_14_out, arg[2], ~arg[3]);  // And
  not not_2 (not_2_out, arg[2]);
  Register #(.Bits(8)) r0 (.D(regin), .C(c_prog), .en(and_9_out), .Q(out_1));
  Register #(.Bits(8)) r1 (.D(regin), .C(c_prog), .en(and_10_out), .Q(out_2));
  Register #(.Bits(8)) r2 (.D(regin), .C(c_prog), .en(and_11_out), .Q(out_3));
  Register #(.Bits(8)) r3 (.D(regin), .C(c_prog), .en(and_12_out), .Q(out_4));
  and and_15 (flf, decoder_2_out_0, not_2_out, arg[3], decoder_3_out_0);
  and and_16 (and_16_out, and_13_out, decoder_3_out_0, decoder_2_out_0);
  and and_17 (and_17_out, and_14_out, decoder_3_out_0, decoder_2_out_0);
  and and_18 (jmp, decoder_3_out_1, decoder_2_out_0);
  and and_19 (inc, decoder_2_out_0, decoder_3_out_2);
  and and_20 (dec, decoder_2_out_0, decoder_3_out_3);
  and and_21 (and_21_out, c_prog, and_17_out);
  and and_22 (clf, decoder_2_out_0, arg[2], arg[3], decoder_3_out_0);
  Multiplexer #(.Selector_Bits(2), .Bits(8)) multiplexer_1 (
    .sel(arg[3:2]), .in_0(out_1), .in_1(out_2), .in_2(out_3), .in_3(out_4), .out(regout_arg0));
  Multiplexer #(.Selector_Bits(2), .Bits(8)) multiplexer_2 (
    .sel(arg[1:0]), .in_0(out_1), .in_1(out_2), .in_2(out_3), .in_3(out_4), .out(regout_arg1));
  LED led_1 (.in(lil));
  LED led_2 (.in(lih));
  LED led_3 (.in(mwr));
  LED led_4 (.in(mrd));
  LED led_5 (.in(mov));
  LED led_6 (.in(bra));
  LED led_7 (.in(rol));
  LED led_8 (.in(eq));
  LED led_9 (.in(gt));
  LED led_10 (.in(add));
  LED led_11 (.in(mul));
  LED led_12 (.in(\and ));
  LED led_13 (.in(\nand ));
  LED led_14 (.in(\or ));
  LED led_15 (.in(\xor ));
  LED led_16 (.in(and_16_out));
  Break brk (.brk(and_21_out));
  LED led_17 (.in(and_17_out));
  LED led_18 (.in(flf));
  LED led_19 (.in(clf));
  LED led_20 (.in(jmp));
  LED led_21 (.in(inc));
  LED led_22 (.in(dec));
  LED led_23 (.in(arg[2]));
  LED led_24 (.in(arg[3]));
  LED led_25 (.in(arg[0]));
  LED led_26 (.in(arg[1]));
  not not_3 (not_3_out, oflag_out);
  not not_4 (not_4_out, mov);
  TransGate #(.Bits(8)) transgate_1 (.A(mov), .nA(not_4_out), .out1(regout_arg1), .out2(regin));
  Add #(.Bits(8)) add_1 (.a(regout_arg0), .b(8'h1), .c_i(oflag_out), .s(add_1_s), .c_o(add_1_c_o));
  Sub #(.Bits(8)) sub_1 (.a(regout_arg0), .b(8'h1), .c_i(oflag_out), .s(sub_1_s), .c_o(sub_1_c_o));
  BarrelShifter #(.Bits(8), .barrelShifterMode("rotate")) barrelshifter_1 (
    .in(regout_arg0), .shift(regout_arg1[3:0]), .out(barrelshifter_1_out));
  Mul mul_1 (.a(regout_arg0[0]), .b(regout_arg1[0]), .mul(mul_1_mul[1:0]));
  assign and_23_out = regout_arg0 & regout_arg1;  // And and_23, 8 bits wide
  assign nand_1_out = ~(regout_arg0 & regout_arg1);  // NAnd nand_1, 8 bits wide
  TransGate #(.Bits(8)) transgate_2 (.A(lil), .nA(not_5_out), .out1({out_1[7:4], arg}), .out2(regin));
  not not_5 (not_5_out, lil);
  TransGate #(.Bits(8)) transgate_3 (.A(lih), .nA(not_6_out), .out1({arg, out_1[3:0]}), .out2(regin));
  not not_6 (not_6_out, lih);
  and and_24 (and_24_out, flf, not_3_out);
  TransGate #(.Bits(8)) transgate_4 (.A(inc), .nA(not_7_out), .out1(add_1_s), .out2(regin));
  and and_25 (and_25_out, add_1_c_o, inc);
  TransGate #(.Bits(8)) transgate_5 (.A(dec), .nA(not_8_out), .out1(sub_1_s), .out2(regin));
  and and_26 (and_26_out, sub_1_c_o, dec);
  BarrelShifter #(.Bits(8), .barrelShifterMode("rotate")) barrelshifter_2 (
    .in(barrelshifter_1_out), .shift(regout_arg1[7:4]), .out(barrelshifter_2_out));
  TransGate #(.Bits(8)) transgate_6 (.A(mul), .nA(not_9_out), .out1(mul_1_mul), .out2(regin));
  TransGate #(.Bits(8)) transgate_7 (.A(\and ), .nA(not_10_out), .out1(and_23_out), .out2(regin));
  TransGate #(.Bits(8)) transgate_8 (.A(\nand ), .nA(not_11_out), .out1(nand_1_out), .out2(regin));
  not not_7 (not_7_out, inc);
  not not_8 (not_8_out, dec);
  TransGate #(.Bits(8)) transgate_9 (.A(rol), .nA(not_12_out), .out1(barrelshifter_2_out), .out2(regin));
  not not_9 (not_9_out, mul);
  not not_10 (not_10_out, \and );
  not not_11 (not_11_out, \nand );
  not not_12 (not_12_out, rol);
  Comparator #(.Bits(8)) comparator_1 (
    .a(regout_arg0), .b(regout_arg1), .eq(comparator_1_eq), .lt(comparator_1_lt));  // open: gt
  Add #(.Bits(8)) add_2 (.a(regout_arg0), .b(regout_arg1), .c_i(oflag_out), .s(add_2_s), .c_o(add_2_c_o));
  or or_6 (or_6_out[0], regout_arg0[0], regout_arg1[0]);
  xor xor_1 (xor_1_out[0], regout_arg0[0], regout_arg1[0]);
  and and_27 (and_27_out, gt, comparator_1_eq);
  and and_28 (and_28_out, comparator_1_lt, eq);
  TransGate #(.Bits(8)) transgate_10 (.A(add), .nA(not_13_out), .out1(add_2_s), .out2(regin));
  and and_29 (and_29_out, add_2_c_o, add);
  not not_13 (not_13_out, add);
  not not_14 (not_14_out, \or );
  TransGate #(.Bits(8)) transgate_11 (.A(\or ), .nA(not_14_out), .out1(or_6_out), .out2(regin));
  not not_15 (not_15_out, \xor );
  TransGate #(.Bits(8)) transgate_12 (.A(\xor ), .nA(not_15_out), .out1(xor_1_out), .out2(regin));
  or or_7 (or_7_out, and_24_out, and_25_out, and_26_out, and_27_out, and_28_out, and_29_out);
  or or_8 (or_8_out, flf, clf, eq, gt, dec, inc);
  Register oflag (.D(or_7_out), .C(c_prog), .en(or_8_out), .Q(oflag_out));
  LED oflag_2 (.in(oflag_out));
  // Pins of 1 and 8 bits meet at regout_arg0
  // Pins of 1 and 8 bits meet at regout_arg1
  // Pins of 2 and 8 bits meet at mul_1_mul
  // Pins of 1 and 8 bits meet at or_6_out
  // Pins of 1 and 8 bits meet at xor_1_out

  // Other names for the same wires on the sheet: arg1[1:0] = arg[1:0]; arg0[1:0] = arg[3:2]; clock = clk;
  //   regout_r0[7:0] = out_1

  // Notes on the sheet:
  //   clock pc loader
  //   contents of rom_1 (hex, n*v repeats v):
  //   22,14,54,26,19,58,4,8a,99,96,86,10,20,84,4
  //   registers
  //   select r0 on lil,lih ops
  //   regin_addr
  //   write enable
  //   op decoder
  //   opcode
  //   arg1 = 0
  //   opcode = 0
  //   todo
  //   nop
  //   brk
  //   lil lih
  //   flf clf mov
  //   alu
  //   oflag
endmodule
