// Digital circuit nna8v0_based_computer_with_screen.dig as structural Verilog
module nna8v0_based_computer_with_screen (
);

  wire and_1_out, and_2_out, clock, firstcycle, mwr;
  wire [7:0] addrbus, mbus;

  and and_1 (and_1_out, ~firstcycle, mwr);  // And
  and and_2 (and_2_out, clock, and_1_out);
  EEPROM #(.AddrBits(8), .isProgramMemory("true"), .Bits(8)) eeprom_1 (
    .A(addrbus), .CS(~clock), .WE(and_2_out), .OE(~and_1_out), .D(mbus));

  // Notes on the sheet:
  //   contents of eeprom_1 (hex, n*v repeats v):
  //   22,58,4c,e,20,1e,33,3e,23,10,54,24,10,1,4,17*0,20,e,14*0,48,65
  //   ,6c,6c,6f,20,57,6f,72,6c,64,21,21,0,0,0,10,2f,58,4d,f0,83,6c,c
  //   ,3e,a,6,63,22,10,4c,47,f,33,5,157*0,48,65,6c,6c,6f,20,57,6f,72
  //   ,6c,64,21,21
endmodule
