// Digital circuit bit-eater-v2.dig as structural Verilog
module bit_eater_v2 (
  input  clk
);

  wire addr_io, addr_mainmem, addr_video, addr_vm, and_1_out, and_2_out, and_5_out, and_8_out, and_9_out,
       and_10_out, and_17_out, and_18_out, and_19_out, and_23_out, and_24_out, and_25_out, and_26_out,
       and_27_out, and_29_out, and_30_out, and_31_out, bra, brk, cal, cal_flag, cary_coadd, cary_cosub,
       co_add, co_and, co_div, co_mod, co_mul, co_not, co_or, co_rol, co_ror, co_shl, co_shr, co_sub,
       comparator_2_eq, comparator_3_eq, comparator_5_eq, comparator_5_lt, d_ff_1_nq, dec, dec_flag,
       decoder_2_out_0, decoder_2_out_1, decoder_3_out_0, decoder_3_out_1, decoder_3_out_2, decoder_3_out_3,
       decoder_4_out_0, decoder_4_out_1, decoder_4_out_2, decoder_4_out_3, dread, dread_video, drw, dwrite,
       dwrite_video, eq, eq_flag, flag_out, flg, flg_flag, gt, gt_flag, inc, inc_flag, jmp, lih, lil, mco,
       mdb, mov, mpb, mrd, multiplexer_3_out, mwr, nclock, nop, not_1_out, not_2_out, not_4_out, not_9_out,
       or_1_out, or_5_out, or_6_out, or_7_out, pc_write, reg_we, sin, xcycle, xcycle_next, \xor ;
  wire [1:0] selreg;
  wire [3:0] arg, co, curop;
  wire [7:0] add_1_s, add_2_s, addrbus, and_32_out, barrelshifter_1_out, barrelshifter_2_out,
       barrelshifter_3_out, barrelshifter_4_out, calbus, databus, db, div_1_q, div_1_r, not_8_out, or_8_out,
       pb, pc, pc_next, r1_q, r2_q, r3_q, regin, regout_arg0, regout_arg1, regout_r0, sub_1_s, sub_2_s, vm,
       xor_1_out;
  wire [15:0] mul_1_mul;
  wire [15:8] addrbus_full;

  GraphicCard #(.graphicHeight(16), .graphicWidth(16), .Bits(8)) graphiccard_1 (
    .A({1'b0, addrbus}), .str(dwrite_video), .C(clk), .ld(dread_video), .B(1'b0), .D(databus));
  // Probe on arg[3:2]
  // Probe on arg[1:0]
  Register #(.Bits(8)) u_curop (.D(databus), .C(clk), .en(~xcycle), .Q({curop, arg}));
  and and_1 (and_1_out, bra, ~flag_out);  // And
  and and_2 (and_2_out, jmp, ~flag_out);  // And
  assign regin = mov ? regout_arg1 : 8'bz;  // Driver driver_1
  // Probe on databus
  // Probe on addrbus
  and and_3 (dwrite, xcycle, mwr);
  and and_4 (dread, xcycle, mrd);
  Decoder #(.Selector_Bits(4)) decoder_1 (
    .sel(curop), .out_0(sin), .out_1(eq), .out_2(gt), .out_3(flg), .out_5(bra), .out_6(mco), .out_7(mwr),
    .out_8(mrd), .out_9(lil), .out_10(lih), .out_11(mov), .out_12(cal), .out_13(\xor ), .out_14(inc),
    .out_15(dec));  // open: out_4
  assign pc_next = and_1_out ? {pc[7:4], arg} : 8'bz;  // Driver driver_2
  assign pc_next = and_2_out ? regout_arg0 : 8'bz;  // Driver driver_3
  // Probe on curop
  // Probe on arg
  or or_1 (or_1_out, mwr, mrd);
  or or_2 (pc_write, and_1_out, and_2_out);
  and and_5 (and_5_out, xcycle, or_1_out);
  Decoder #(.Selector_Bits(2)) decoder_2 (
    .sel(arg[3:2]), .out_0(decoder_2_out_0), .out_1(decoder_2_out_1));  // open: out_2, out_3
  Decoder #(.Selector_Bits(2)) decoder_3 (
    .sel(arg[1:0]), .out_0(decoder_3_out_0), .out_1(decoder_3_out_1), .out_2(decoder_3_out_2),
    .out_3(decoder_3_out_3));
  not not_1 (not_1_out, flag_out);
  not not_2 (not_2_out, arg[2]);
  assign addrbus = and_5_out ? regout_arg1 : 8'bz;  // Driver driver_4
  assign regin = dread ? databus : 8'bz;  // Driver driver_5
  assign databus = dwrite ? regout_arg0 : 8'bz;  // Driver driver_6
  Comparator #(.Bits(8)) comparator_1 (.a(addrbus_full), .b(8'hfe), .eq(addr_video));  // open: gt, lt
  and and_6 (dwrite_video, addr_video, dwrite);
  and and_7 (dread_video, addr_video, dread);
  and and_8 (and_8_out, sin, decoder_3_out_0);
  and and_9 (and_9_out, not_1_out, not_2_out);
  and and_10 (and_10_out, arg[3], arg[2]);
  and and_11 (nop, and_8_out, decoder_2_out_0);
  and and_12 (brk, and_8_out, decoder_2_out_1);
  and and_13 (jmp, decoder_3_out_1, sin);
  and and_14 (mpb, decoder_3_out_2, sin);
  and and_15 (mdb, decoder_3_out_3, sin);
  or or_3 (flg_flag, and_9_out, and_10_out);
  Comparator #(.Bits(8)) comparator_2 (.a(addrbus), .b(8'h3), .eq(comparator_2_eq));  // open: gt, lt
  assign regin = lil ? {regout_r0[7:4], arg} : 8'bz;  // Driver driver_7
  assign regin = lih ? {arg, regout_r0[3:0]} : 8'bz;  // Driver driver_8
  and and_16 (addr_vm, comparator_2_eq, addr_io);
  or or_4 (drw, dwrite, dread);
  assign addrbus_full = drw ? db : 8'bz;  // Driver driver_9
  assign addrbus_full = ~drw ? pb : 8'bz;  // DriverInvSel driverinvsel_1
  and and_17 (and_17_out, clk, dwrite);
  and and_18 (and_18_out, ~xcycle, mrd);  // And
  or or_5 (or_5_out, lil, lih);
  and and_19 (and_19_out, dwrite, addr_vm);
  and and_20 (reg_we, curop[3], ~and_18_out);  // And
  and and_21 (selreg[1], arg[3], ~or_5_out);  // And
  and and_22 (selreg[0], arg[2], ~or_5_out);  // And
  EEPROM #(.AddrBits(13), .isProgramMemory("true"), .Bits(8)) eeprom_1 (
    .A({1'b0, addrbus_full[11:8], addrbus}), .CS(addr_mainmem), .WE(and_17_out), .OE(~dwrite), .D(databus));
  Register #(.Bits(8)) u_vm (.D(databus), .C(clk), .en(and_19_out), .Q(vm));
  Decoder #(.Selector_Bits(2)) decoder_4 (
    .sel(selreg), .out_0(decoder_4_out_0), .out_1(decoder_4_out_1), .out_2(decoder_4_out_2),
    .out_3(decoder_4_out_3));
  and and_23 (and_23_out, decoder_4_out_0, reg_we);
  and and_24 (and_24_out, decoder_4_out_1, reg_we);
  and and_25 (and_25_out, decoder_4_out_2, reg_we);
  and and_26 (and_26_out, decoder_4_out_3, reg_we);
  and and_27 (and_27_out, dread, addr_vm);
  Comparator #(.Bits(4)) comparator_3 (.a(addrbus_full[15:12]), .b(4'b1111), .eq(comparator_3_eq));  // open: gt, lt
  Comparator #(.Bits(8)) comparator_4 (.a(addrbus_full), .b({8{1'b1}}), .eq(addr_io));  // open: gt, lt
  assign databus = and_27_out ? vm : 8'bz;  // Driver driver_10
  not not_3 (addr_mainmem, comparator_3_eq);
  PullDown #(.Bits(8)) pulldown_1 (.out(regin));
  Register #(.Bits(8)) r0 (.D(regin), .C(nclock), .en(and_23_out), .Q(regout_r0));
  Register #(.Bits(8)) r1 (.D(regin), .C(nclock), .en(and_24_out), .Q(r1_q));
  Register #(.Bits(8)) r2 (.D(regin), .C(nclock), .en(and_25_out), .Q(r2_q));
  Register #(.Bits(8)) r3 (.D(regin), .C(nclock), .en(and_26_out), .Q(r3_q));
  Register #(.Bits(8)) u_pb (.D(regout_arg0), .C(nclock), .en(mpb), .Q(pb));
  Register #(.Bits(8)) u_db (.D(regout_arg0), .C(nclock), .en(mdb), .Q(db));
  Register #(.Bits(4)) u_co (.D(arg), .C(nclock), .en(mco), .Q(co));
  // Probe on regout_r0
  // Probe on r1_q
  // Probe on r2_q
  // Probe on r3_q
  // Probe on pb
  Break u_mpb (.brk(mpb));
  // Probe on db
  Break u_mdb (.brk(mdb));
  // Probe on co
  Multiplexer #(.Selector_Bits(2), .Bits(8)) multiplexer_1 (
    .sel(arg[3:2]), .in_0(regout_r0), .in_1(r1_q), .in_2(r2_q), .in_3(r3_q), .out(regout_arg0));
  Multiplexer #(.Selector_Bits(2), .Bits(8)) multiplexer_2 (
    .sel(arg[1:0]), .in_0(regout_r0), .in_1(r1_q), .in_2(r2_q), .in_3(r3_q), .out(regout_arg1));
  CounterPreset #(.Bits(8), .isProgramCounter("true")) u_PC (
    .en(~xcycle), .C(clk), .dir(1'b0), .in(pc_next), .ld(pc_write), .clr(mpb), .out(pc));  // open: ovf
  not not_4 (not_4_out, xcycle);
  or or_6 (or_6_out, mrd, pc_write, mwr);
  assign addrbus = not_4_out ? pc : 8'bz;  // Driver driver_11
  and and_28 (xcycle_next, d_ff_1_nq, or_6_out);
  Decoder #(.Selector_Bits(4)) decoder_5 (
    .sel(co), .out_0(co_add), .out_1(co_sub), .out_2(co_mul), .out_3(co_div), .out_4(co_shl), .out_5(co_shr),
    .out_6(co_rol), .out_7(co_ror), .out_8(co_and), .out_9(co_or), .out_10(co_not), .out_11(co_mod));  // open: out_12, out_13, out_14, out_15
  D_FF d_ff_1 (.D(xcycle_next), .C(~clk), .Q(xcycle), .nQ(d_ff_1_nq));
  Add #(.Bits(8)) add_1 (.a(regout_arg0), .b(regout_arg1), .c_i(flag_out), .s(add_1_s), .c_o(cary_coadd));
  Sub #(.Bits(8)) sub_1 (.a(regout_arg0), .b(regout_arg1), .c_i(flag_out), .s(sub_1_s), .c_o(cary_cosub));
  Mul #(.Bits(8)) mul_1 (.a(regout_arg0), .b(regout_arg1), .mul(mul_1_mul));
  Div #(.Bits(8)) div_1 (.a(regout_arg0), .b(regout_arg1), .q(div_1_q), .r(div_1_r));
  // Probe on pc
  // Probe on addrbus
  // Probe on databus
  // Probe on xcycle
  Break u_brk (.brk(brk));
  LED led_1 (.in(xcycle));
  assign regin = cal ? calbus : 8'bz;  // Driver driver_12
  Comparator #(.Bits(8)) comparator_5 (
    .a(regout_arg0), .b(regout_arg1), .eq(comparator_5_eq), .lt(comparator_5_lt));  // open: gt
  assign xor_1_out = regout_arg0 ^ regout_arg1;  // XOr xor_1, 8 bits wide
  Add #(.Bits(8)) add_2 (.a(regout_arg0), .b({{6{1'b0}}, arg[1:0]}), .c_i(1'b1), .s(add_2_s), .c_o(inc_flag));
  Sub #(.Bits(8)) sub_2 (.a(regout_arg0), .b({{6{1'b0}}, arg[1:0]}), .c_i(1'b1), .s(sub_2_s), .c_o(dec_flag));
  not not_5 (nclock, clk);
  not not_6 (eq_flag, comparator_5_eq);
  not not_7 (gt_flag, comparator_5_lt);
  assign regin = inc ? add_2_s : 8'bz;  // Driver driver_13
  assign regin = dec ? sub_2_s : 8'bz;  // Driver driver_14
  assign calbus = co_add ? add_1_s : 8'bz;  // Driver driver_15
  assign calbus = co_sub ? sub_1_s : 8'bz;  // Driver driver_16
  assign calbus = co_mul ? mul_1_mul[7:0] : 8'bz;  // Driver driver_17
  assign calbus = co_div ? div_1_q : 8'bz;  // Driver driver_18
  assign calbus = co_mod ? div_1_r : 8'bz;  // Driver driver_19
  assign regin = \xor  ? xor_1_out : 8'bz;  // Driver driver_20
  or or_7 (or_7_out, co_add, co_sub);
  Multiplexer #(.Selector_Bits(4)) multiplexer_3 (
    .sel(curop), .in_0(flag_out), .in_1(eq_flag), .in_2(gt_flag), .in_3(flg_flag), .in_4(flag_out),
    .in_5(flag_out), .in_6(flag_out), .in_7(flag_out), .in_8(flag_out), .in_9(flag_out), .in_10(flag_out),
    .in_11(flag_out), .in_12(cal_flag), .in_13(flag_out), .in_14(inc_flag), .in_15(dec_flag),
    .out(multiplexer_3_out));
  and and_29 (and_29_out, co_add, cary_coadd);
  and and_30 (and_30_out, co_sub, cary_cosub);
  and and_31 (and_31_out, ~or_7_out, flag_out);  // And
  assign and_32_out = regout_arg0 & regout_arg1;  // And and_32, 8 bits wide
  assign or_8_out = regout_arg0 | regout_arg1;  // Or or_8, 8 bits wide
  assign not_8_out = ~regout_arg0;  // Not not_8, 8 bits wide
  BarrelShifter #(.Bits(8)) barrelshifter_1 (.in(regout_arg0), .shift(regout_arg1[3:0]), .out(barrelshifter_1_out));
  BarrelShifter #(.Bits(8), .direction("right")) barrelshifter_2 (
    .in(regout_arg0), .shift(regout_arg1[3:0]), .out(barrelshifter_2_out));
  BarrelShifter #(.Bits(8), .barrelShifterMode("rotate")) barrelshifter_3 (
    .in(regout_arg0), .shift(regout_arg1[3:0]), .out(barrelshifter_3_out));
  BarrelShifter #(.Bits(8), .barrelShifterMode("rotate")) barrelshifter_4 (
    .in(regout_arg0), .shift(regout_arg1[3:0]), .out(barrelshifter_4_out));
  not not_9 (not_9_out, clk);
  or or_9 (cal_flag, and_29_out, and_30_out, and_31_out);
  assign calbus = co_and ? and_32_out : 8'bz;  // Driver driver_21
  assign calbus = co_or ? or_8_out : 8'bz;  // Driver driver_22
  assign calbus = co_not ? not_8_out : 8'bz;  // Driver driver_23
  assign calbus = co_shl ? barrelshifter_1_out : 8'bz;  // Driver driver_24
  assign calbus = co_shr ? barrelshifter_2_out : 8'bz;  // Driver driver_25
  assign calbus = co_ror ? barrelshifter_3_out : 8'bz;  // Driver driver_26
  assign calbus = co_rol ? barrelshifter_4_out : 8'bz;  // Driver driver_27
  Register flag (.D(multiplexer_3_out), .C(not_9_out), .en(1'b1), .Q(flag_out));

  // Other names for the same wires on the sheet: arg1[1:0] = arg[1:0]; arg0[1:0] = arg[3:2];
  //   addrbus_full[7:0] = addrbus; bankbus[7:0] = addrbus_full; clock = clk

  // Notes on the sheet:
  //   clk: Hz: 2000
  //   operations
  //   op decoder
  //   jmp bra
  //   mov
  //   mwr, mrd
  //   video
  //   flg
  //   addr decoding
  //   sin
  //   lil lih
  //   main mem
  //   registers
  //   for mrd instruction only set reg_we on the xcylce
  //   select r0 on lil,lih ops
  //   contents of eeprom_1 (hex, n*v repeats v):
  //   91,a7,b4,90,a7,74,85,0,34,96,a2,bc,9f,a0,d,d0,4,e0,50,34,90,a7
  //   ,84,e4,74,85,d0,14,30,98,a0,1,34,d0,1,0,0,0,bc,9e,a6,7c,9f,a6
  //   ,74,df,d5,0,a6,9f,88,60,cb,91,a0,3,8a,9e,af,3,d0,c1,78,d0,3,bb
  //   ,6b,94,a0,cc,f0,13,be,30,5f,9b,a0,60,c4,34,ec,e4,9f,a0,13,30,5c
  //   ,34,9e,a6,80,1,90,a3,1,15*0,f,c0,79,70,40,a0,a0,b0,e0,d0,b0,c0
  //   ,a0,30,132*0,ff,ff,ff,0,ff,0,ff,0,ff,ff,ff,0,ff,0,ff,0,ff,ff,ff
  //   ,0,ff,0,4*ff,0,10*ff,0,0,0,ff,0,0,0,6*ff,0,0,ff,0,ff,0,ff,0,ff
  //   ,0,ff,ff,0,0,7*ff,0,ff,0,0,0,9*ff,0,0,0,ff,ff,ff,0,ff,0,0,0,5*ff
  //   ,0,0,0,ff,0,0,6*ff,0,ff,0,ff,0,ff,0,ff,ff,ff,0,ff,0,ff,0,4*ff
  //   ,0,ff,ff,0,0,ff,ff,0,8*ff,0,0,0,ff,ff,0,0,6*ff,0,0,0,ff,0,0,0
  //   ,ff,0,0,0,9*ff,0,0,ff,ff,0,0,10*ff,0,0,6*ff,0,ff,0,ff,0,0,ff,ff
  //   ,0,0,ff,ff,0,6*ff
  //   pc,clock
  //   alu
  //   inc dec
  //   arithmetic
  //   calbus link
  //   flag
  //   flag ctrl
  //   logical
  //   shifts
endmodule
