// Digital circuit bus-transiever.dig as structural Verilog
module bus_transiever (
  input  A,
  input  DIR,
  input  OE,
  input  B
);

  wire and_1_out, and_2_out;

  and and_1 (and_1_out, DIR, ~OE);  // And
  assign B = and_1_out ? A : 1'bz;  // Driver driver_1
  assign A = and_2_out ? B : 1'bz;  // Driver driver_2
  and and_2 (and_2_out, ~OE, ~DIR);  // And
endmodule
