// Digital circuit display_test.dig as structural Verilog
module display_test (
  input  [7:0] y,
  input  [7:0] x
);

  // PolarityAwareLED polarityawareled_1: pin names not known; wires that end beside it: x[0], y[7]
  // PolarityAwareLED polarityawareled_2: pin names not known; wires that end beside it: x[0], y[6]
  // PolarityAwareLED polarityawareled_3: pin names not known; wires that end beside it: x[0], y[5]
  // PolarityAwareLED polarityawareled_4: pin names not known; wires that end beside it: x[0], y[4]
  // PolarityAwareLED polarityawareled_5: pin names not known; wires that end beside it: x[0], y[3]
  // PolarityAwareLED polarityawareled_6: pin names not known; wires that end beside it: x[0], y[2]
  // PolarityAwareLED polarityawareled_7: pin names not known; wires that end beside it: x[0], y[1]
  // PolarityAwareLED polarityawareled_8: pin names not known; wires that end beside it: x[0], y[0], x[0]
  // PolarityAwareLED polarityawareled_9: pin names not known; wires that end beside it: x[1], y[7]
  // PolarityAwareLED polarityawareled_10: pin names not known; wires that end beside it: x[1], y[6]
  // PolarityAwareLED polarityawareled_11: pin names not known; wires that end beside it: x[1], y[5]
  // PolarityAwareLED polarityawareled_12: pin names not known; wires that end beside it: x[1], y[4]
  // PolarityAwareLED polarityawareled_13: pin names not known; wires that end beside it: x[1], y[3]
  // PolarityAwareLED polarityawareled_14: pin names not known; wires that end beside it: x[1], y[2]
  // PolarityAwareLED polarityawareled_15: pin names not known; wires that end beside it: x[1], y[1]
  // PolarityAwareLED polarityawareled_16: pin names not known; wires that end beside it: x[1], y[0], x[1]
  // PolarityAwareLED polarityawareled_17: pin names not known; wires that end beside it: x[2], y[7]
  // PolarityAwareLED polarityawareled_18: pin names not known; wires that end beside it: x[3], y[7]
  // PolarityAwareLED polarityawareled_19: pin names not known; wires that end beside it: x[2], y[6]
  // PolarityAwareLED polarityawareled_20: pin names not known; wires that end beside it: x[3], y[6]
  // PolarityAwareLED polarityawareled_21: pin names not known; wires that end beside it: x[2], y[5]
  // PolarityAwareLED polarityawareled_22: pin names not known; wires that end beside it: x[3], y[5]
  // PolarityAwareLED polarityawareled_23: pin names not known; wires that end beside it: x[2], y[4]
  // PolarityAwareLED polarityawareled_24: pin names not known; wires that end beside it: x[3], y[4]
  // PolarityAwareLED polarityawareled_25: pin names not known; wires that end beside it: x[2], y[3]
  // PolarityAwareLED polarityawareled_26: pin names not known; wires that end beside it: x[3], y[3]
  // PolarityAwareLED polarityawareled_27: pin names not known; wires that end beside it: x[2], y[2]
  // PolarityAwareLED polarityawareled_28: pin names not known; wires that end beside it: x[3], y[2]
  // PolarityAwareLED polarityawareled_29: pin names not known; wires that end beside it: x[2], y[1]
  // PolarityAwareLED polarityawareled_30: pin names not known; wires that end beside it: x[3], y[1]
  // PolarityAwareLED polarityawareled_31: pin names not known; wires that end beside it: x[2], y[0], x[2]
  // PolarityAwareLED polarityawareled_32: pin names not known; wires that end beside it: x[3], y[0], x[3]
  // PolarityAwareLED polarityawareled_33: pin names not known; wires that end beside it: x[4], y[7]
  // PolarityAwareLED polarityawareled_34: pin names not known; wires that end beside it: x[4], y[6]
  // PolarityAwareLED polarityawareled_35: pin names not known; wires that end beside it: x[4], y[5]
  // PolarityAwareLED polarityawareled_36: pin names not known; wires that end beside it: x[4], y[4]
  // PolarityAwareLED polarityawareled_37: pin names not known; wires that end beside it: x[4], y[3]
  // PolarityAwareLED polarityawareled_38: pin names not known; wires that end beside it: x[4], y[2]
  // PolarityAwareLED polarityawareled_39: pin names not known; wires that end beside it: x[4], y[1]
  // PolarityAwareLED polarityawareled_40: pin names not known; wires that end beside it: x[4], y[0], x[4]
  // PolarityAwareLED polarityawareled_41: pin names not known; wires that end beside it: x[5], y[7]
  // PolarityAwareLED polarityawareled_42: pin names not known; wires that end beside it: x[5], y[6]
  // PolarityAwareLED polarityawareled_43: pin names not known; wires that end beside it: x[5], y[5]
  // PolarityAwareLED polarityawareled_44: pin names not known; wires that end beside it: x[5], y[4]
  // PolarityAwareLED polarityawareled_45: pin names not known; wires that end beside it: x[5], y[3]
  // PolarityAwareLED polarityawareled_46: pin names not known; wires that end beside it: x[5], y[2]
  // PolarityAwareLED polarityawareled_47: pin names not known; wires that end beside it: x[5], y[1]
  // PolarityAwareLED polarityawareled_48: pin names not known; wires that end beside it: x[5], y[0], x[5]
  // PolarityAwareLED polarityawareled_49: pin names not known; wires that end beside it: x[6], y[7]
  // PolarityAwareLED polarityawareled_50: pin names not known; wires that end beside it: x[7], y[7]
  // PolarityAwareLED polarityawareled_51: pin names not known; wires that end beside it: x[6], y[6]
  // PolarityAwareLED polarityawareled_52: pin names not known; wires that end beside it: x[7], y[6]
  // PolarityAwareLED polarityawareled_53: pin names not known; wires that end beside it: x[6], y[5]
  // PolarityAwareLED polarityawareled_54: pin names not known; wires that end beside it: x[7], y[5]
  // PolarityAwareLED polarityawareled_55: pin names not known; wires that end beside it: x[6], y[4]
  // PolarityAwareLED polarityawareled_56: pin names not known; wires that end beside it: x[7], y[4]
  // PolarityAwareLED polarityawareled_57: pin names not known; wires that end beside it: x[6], y[3]
  // PolarityAwareLED polarityawareled_58: pin names not known; wires that end beside it: x[7], y[3]
  // PolarityAwareLED polarityawareled_59: pin names not known; wires that end beside it: x[6], y[2]
  // PolarityAwareLED polarityawareled_60: pin names not known; wires that end beside it: x[7], y[2]
  // PolarityAwareLED polarityawareled_61: pin names not known; wires that end beside it: x[6], y[1]
  // PolarityAwareLED polarityawareled_62: pin names not known; wires that end beside it: x[7], y[1]
  // PolarityAwareLED polarityawareled_63: pin names not known; wires that end beside it: x[6], y[0], x[6]
  // PolarityAwareLED polarityawareled_64: pin names not known; wires that end beside it: x[7], y[0], x[7]
endmodule
