// Digital circuit ram.dig as structural Verilog
module ram (
  input  [7:0] D,
  input  [14:0] A,
  input  [7:0] WE,
  input  [7:0] OE
);

  wire [7:0] driver_1_out, ramasync_1_q;

  RAMAsync #(.AddrBits(15), .Bits(8)) ramasync_1 (.A(A), .D(driver_1_out), .we(WE[0]), .Q(ramasync_1_q));
  assign driver_1_out = WE[0] ? D : 8'bz;  // Driver driver_1
  assign D = OE[0] ? ramasync_1_q : 8'bz;  // Driver driver_2
  // Pins of 1 and 8 bits meet at WE
  // Pins of 1 and 8 bits meet at OE
endmodule
