// Digital circuit barrel_shifter8.dig as structural Verilog
module barrel_shifter8 (
  input  [7:0] in,
  input  [2:0] shift,
  input  roll,
  output [7:0] out
);

  wire and_1_out, and_2_out, and_3_out, and_4_out, and_5_out, and_6_out;

  and and_1 (and_1_out, in[0], roll);
  buf and_2 (and_2_out, roll);  // And open: In_1
  buf and_3 (and_3_out, roll);  // And open: In_1
  buf and_4 (and_4_out, roll);  // And open: In_1
  buf and_5 (and_5_out, roll);  // And open: In_1
  buf and_6 (and_6_out, roll);  // And open: In_1
  Multiplexer #(.Selector_Bits(3)) multiplexer_1 (
    .sel(shift), .in_0(in[0]), .in_1(in[1]), .in_2(in[2]), .in_3(in[3]), .in_4(in[4]), .in_5(in[5]),
    .in_6(in[6]), .in_7(in[7]));  // open: out
  Multiplexer #(.Selector_Bits(3)) multiplexer_2 (
    .sel(shift), .in_0(in[1]), .in_1(in[2]), .in_2(in[3]), .in_3(in[4]), .in_4(in[5]), .in_5(in[6]),
    .in_6(in[7]), .in_7(and_1_out));  // open: out
  Multiplexer #(.Selector_Bits(3)) multiplexer_3 (
    .sel(shift), .in_0(in[2]), .in_1(in[3]), .in_2(in[4]), .in_3(in[5]), .in_4(in[6]), .in_5(in[7]),
    .in_6(and_2_out), .in_7(and_3_out));  // open: out
  Multiplexer #(.Selector_Bits(3)) multiplexer_4 (
    .sel(shift), .in_0(in[3]), .in_1(in[4]), .in_2(in[5]), .in_3(in[6]), .in_4(in[7]), .in_5(and_4_out),
    .in_6(and_5_out), .in_7(and_6_out));  // open: out
endmodule
