// Digital circuit dlatch_shifter8.dig as structural Verilog
module dlatch_shifter8 (
  input  clk,
  input  in,
  output [7:0] out,
  output ovf
);

  D_FF d_ff_1 (.D(in), .C(clk), .nQ(out[0]));  // open: Q
  D_FF d_ff_2 (.D(out[0]), .C(clk), .nQ(out[1]));  // open: Q
  D_FF d_ff_3 (.D(out[1]), .C(clk), .nQ(out[2]));  // open: Q
  D_FF d_ff_4 (.D(out[2]), .C(clk), .nQ(out[3]));  // open: Q
  D_FF d_ff_5 (.D(out[3]), .C(clk), .nQ(out[4]));  // open: Q
  D_FF d_ff_6 (.D(out[4]), .C(clk), .nQ(out[5]));  // open: Q
  D_FF d_ff_7 (.D(out[5]), .C(clk), .nQ(out[6]));  // open: Q
  D_FF d_ff_8 (.D(out[6]), .C(clk), .nQ(out[7]));  // open: Q
  // Pins of 1 and 8 bits meet at out

  assign ovf = out[7];
endmodule
