// Digital circuit nna8v2_mpu.dig as structural Verilog
module nna8v2_mpu (
  input  clk,
  input  [15:0] A,
  input  rst,
  output [7:0] D,
  output dread,
  output dwrite,
  output brk
);

  wire and_1_out, and_2_out, and_5_out, and_6_out, and_7_out, and_8_out, and_14_out, and_18_out, and_19_out,
       and_20_out, and_21_out, and_23_out, and_24_out, and_25_out, bra, cal, cal_flag, cary_coadd,
       cary_cosub, co_add, co_and, co_div, co_mod, co_mul, co_not, co_or, co_rol, co_ror, co_shl, co_shr,
       co_sub, comparator_1_eq, comparator_1_lt, d_ff_1_nq, dec, dec_flag, decoder_2_out_0, decoder_2_out_1,
       decoder_3_out_0, decoder_3_out_1, decoder_3_out_2, decoder_3_out_3, decoder_4_out_0, decoder_4_out_1,
       decoder_4_out_2, decoder_4_out_3, drw, eq, eq_flag, flag_out, flg, flg_flag, gt, gt_flag, inc,
       inc_flag, jmp, lih, lil, mco, mdb, mov, mpb, mrd, multiplexer_3_out, mwr, nclock, nop, not_1_out,
       not_2_out, not_3_out, not_5_out, not_6_out, not_9_out, or_1_out, or_2_out, or_6_out, or_7_out,
       or_8_out, or_9_out, or_10_out, or_11_out, or_12_out, or_14_out, or_15_out, or_16_out, pc_write,
       reg_we, sin, xcycle, xcycle_next, \xor ;
  wire [1:0] selreg;
  wire [3:0] arg, co, curop;
  wire [7:0] add_1_s, add_2_s, and_26_out, barrelshifter_1_out, barrelshifter_2_out, barrelshifter_3_out,
       barrelshifter_4_out, calbus, databus, db, div_1_q, div_1_r, not_10_out, or_17_out, pb, pc, pc_next,
       r1_q, r2_q, r3_q, regin, regout_arg0, regout_arg1, regout_r0, sub_1_s, sub_2_s, xor_1_out;
  wire [15:0] mul_1_mul;

  not not_1 (not_1_out, xcycle);
  or or_1 (or_1_out, rst, not_1_out);
  // Probe on arg[3:2]
  // Probe on arg[1:0]
  Register #(.Bits(8)) u_curop (.D(databus), .C(clk), .en(or_1_out), .Q({curop, arg}));
  and and_1 (and_1_out, bra, ~flag_out);  // And
  and and_2 (and_2_out, jmp, ~flag_out);  // And
  assign regin = mov ? regout_arg1 : 8'bz;  // Driver driver_1
  // Probe on databus
  // Probe on A[7:0]
  and and_3 (dwrite, xcycle, mwr);
  and and_4 (dread, xcycle, mrd);
  Decoder #(.Selector_Bits(4)) decoder_1 (
    .sel(curop), .out_0(sin), .out_1(eq), .out_2(gt), .out_3(flg), .out_5(bra), .out_6(mco), .out_7(mwr),
    .out_8(mrd), .out_9(lil), .out_10(lih), .out_11(mov), .out_12(cal), .out_13(\xor ), .out_14(inc),
    .out_15(dec));  // open: out_4
  assign pc_next = and_1_out ? {pc[7:4], arg} : 8'bz;  // Driver driver_2
  assign pc_next = and_2_out ? regout_arg0 : 8'bz;  // Driver driver_3
  // Probe on curop
  // Probe on arg
  or or_2 (or_2_out, mwr, mrd);
  or or_3 (pc_write, and_1_out, and_2_out);
  and and_5 (and_5_out, xcycle, or_2_out);
  Decoder #(.Selector_Bits(2)) decoder_2 (
    .sel(arg[3:2]), .out_0(decoder_2_out_0), .out_1(decoder_2_out_1));  // open: out_2, out_3
  Decoder #(.Selector_Bits(2)) decoder_3 (
    .sel(arg[1:0]), .out_0(decoder_3_out_0), .out_1(decoder_3_out_1), .out_2(decoder_3_out_2),
    .out_3(decoder_3_out_3));
  not not_2 (not_2_out, flag_out);
  not not_3 (not_3_out, arg[2]);
  assign A[7:0] = and_5_out ? regout_arg1 : 8'bz;  // Driver driver_4
  assign regin = dread ? databus : 8'bz;  // Driver driver_5
  assign databus = dwrite ? regout_arg0 : 8'bz;  // Driver driver_6
  and and_6 (and_6_out, sin, decoder_3_out_0);
  and and_7 (and_7_out, not_2_out, not_3_out);
  and and_8 (and_8_out, arg[3], arg[2]);
  and and_9 (nop, and_6_out, decoder_2_out_0);
  and and_10 (brk, and_6_out, decoder_2_out_1);
  and and_11 (jmp, decoder_3_out_1, sin);
  and and_12 (mpb, decoder_3_out_2, sin);
  and and_13 (mdb, decoder_3_out_3, sin);
  or or_4 (flg_flag, and_7_out, and_8_out);
  assign regin = lil ? {regout_r0[7:4], arg} : 8'bz;  // Driver driver_7
  assign regin = lih ? {arg, regout_r0[3:0]} : 8'bz;  // Driver driver_8
  or or_5 (drw, dwrite, dread);
  assign A[15:8] = drw ? db : 8'bz;  // Driver driver_9
  assign A[15:8] = ~drw ? pb : 8'bz;  // DriverInvSel driverinvsel_1
  and and_14 (and_14_out, ~xcycle, mrd);  // And
  not not_4 (nclock, clk);
  or or_6 (or_6_out, lil, lih);
  and and_15 (reg_we, curop[3], ~and_14_out);  // And
  and and_16 (selreg[1], arg[3], ~or_6_out);  // And
  and and_17 (selreg[0], arg[2], ~or_6_out);  // And
  Decoder #(.Selector_Bits(2)) decoder_4 (
    .sel(selreg), .out_0(decoder_4_out_0), .out_1(decoder_4_out_1), .out_2(decoder_4_out_2),
    .out_3(decoder_4_out_3));
  not not_5 (not_5_out, rst);
  assign databus = not_5_out ? D : 8'bz;  // Driver driver_10
  PullDown #(.Bits(8)) pulldown_1 (.out(databus));
  PullDown #(.Bits(8)) pulldown_2 (.out(pc_next));
  or or_7 (or_7_out, pc_write, rst);
  and and_18 (and_18_out, decoder_4_out_0, reg_we);
  and and_19 (and_19_out, decoder_4_out_1, reg_we);
  and and_20 (and_20_out, decoder_4_out_2, reg_we);
  and and_21 (and_21_out, decoder_4_out_3, reg_we);
  or or_8 (or_8_out, and_18_out, rst);
  or or_9 (or_9_out, and_19_out, rst);
  or or_10 (or_10_out, and_20_out, rst);
  or or_11 (or_11_out, and_21_out, rst);
  or or_12 (or_12_out, rst, mpb);
  or or_13 (nclock, rst, mdb);
  or or_14 (or_14_out, rst, mco);
  CounterPreset #(.Bits(8), .isProgramCounter("true")) u_PC (
    .en(~xcycle), .C(clk), .dir(1'b0), .in(pc_next), .ld(or_7_out), .clr(mpb), .out(pc));  // open: ovf
  not not_6 (not_6_out, xcycle);
  or or_15 (or_15_out, mrd, pc_write, mwr);
  PullDown #(.Bits(8)) pulldown_3 (.out(regin));
  Register #(.Bits(8)) r0 (.D(regin), .C(nclock), .en(or_8_out), .Q(regout_r0));
  Register #(.Bits(8)) r1 (.D(regin), .C(nclock), .en(or_9_out), .Q(r1_q));
  Register #(.Bits(8)) r2 (.D(regin), .C(nclock), .en(or_10_out), .Q(r2_q));
  Register #(.Bits(8)) r3 (.D(regin), .C(nclock), .en(or_11_out), .Q(r3_q));
  Register #(.Bits(8)) u_pb (.D(regout_arg0), .C(nclock), .en(or_12_out), .Q(pb));
  Register #(.Bits(8)) u_db (.D(regout_arg0), .C(nclock), .en(nclock), .Q(db));
  Register #(.Bits(4)) u_co (.D(arg), .C(nclock), .en(or_14_out), .Q(co));
  assign A[7:0] = not_6_out ? pc : 8'bz;  // Driver driver_11
  and and_22 (xcycle_next, d_ff_1_nq, or_15_out);
  // Probe on regout_r0
  // Probe on r1_q
  // Probe on r2_q
  // Probe on r3_q
  // Probe on pb
  Break u_mpb (.brk(or_12_out));
  // Probe on db
  Break u_mdb (.brk(nclock));
  // Probe on co
  D_FF d_ff_1 (.D(xcycle_next), .C(~clk), .Q(xcycle), .nQ(d_ff_1_nq));
  Multiplexer #(.Selector_Bits(2), .Bits(8)) multiplexer_1 (
    .sel(arg[3:2]), .in_0(regout_r0), .in_1(r1_q), .in_2(r2_q), .in_3(r3_q), .out(regout_arg0));
  Multiplexer #(.Selector_Bits(2), .Bits(8)) multiplexer_2 (
    .sel(arg[1:0]), .in_0(regout_r0), .in_1(r1_q), .in_2(r2_q), .in_3(r3_q), .out(regout_arg1));
  // Probe on pc
  // Probe on A[7:0]
  // Probe on databus
  // Probe on xcycle
  LED led_1 (.in(xcycle));
  Decoder #(.Selector_Bits(4)) decoder_5 (
    .sel(co), .out_0(co_add), .out_1(co_sub), .out_2(co_mul), .out_3(co_div), .out_4(co_shl), .out_5(co_shr),
    .out_6(co_rol), .out_7(co_ror), .out_8(co_and), .out_9(co_or), .out_10(co_not), .out_11(co_mod));  // open: out_12, out_13, out_14, out_15
  Add #(.Bits(8)) add_1 (.a(regout_arg0), .b(regout_arg1), .c_i(flag_out), .s(add_1_s), .c_o(cary_coadd));
  Sub #(.Bits(8)) sub_1 (.a(regout_arg0), .b(regout_arg1), .c_i(flag_out), .s(sub_1_s), .c_o(cary_cosub));
  Mul #(.Bits(8)) mul_1 (.a(regout_arg0), .b(regout_arg1), .mul(mul_1_mul));
  Div #(.Bits(8)) div_1 (.a(regout_arg0), .b(regout_arg1), .q(div_1_q), .r(div_1_r));
  assign regin = cal ? calbus : 8'bz;  // Driver driver_12
  Comparator #(.Bits(8)) comparator_1 (
    .a(regout_arg0), .b(regout_arg1), .eq(comparator_1_eq), .lt(comparator_1_lt));  // open: gt
  assign xor_1_out = regout_arg0 ^ regout_arg1;  // XOr xor_1, 8 bits wide
  Add #(.Bits(8)) add_2 (.a(regout_arg0), .b({{6{1'b0}}, arg[1:0]}), .c_i(1'b1), .s(add_2_s), .c_o(inc_flag));
  Sub #(.Bits(8)) sub_2 (.a(regout_arg0), .b({{6{1'b0}}, arg[1:0]}), .c_i(1'b1), .s(sub_2_s), .c_o(dec_flag));
  Multiplexer #(.Selector_Bits(4)) multiplexer_3 (
    .sel(curop), .in_0(flag_out), .in_1(eq_flag), .in_2(gt_flag), .in_3(flg_flag), .in_4(flag_out),
    .in_5(flag_out), .in_6(flag_out), .in_7(flag_out), .in_8(flag_out), .in_9(flag_out), .in_10(flag_out),
    .in_11(flag_out), .in_12(cal_flag), .in_13(flag_out), .in_14(inc_flag), .in_15(dec_flag),
    .out(multiplexer_3_out));
  not not_7 (eq_flag, comparator_1_eq);
  not not_8 (gt_flag, comparator_1_lt);
  assign regin = inc ? add_2_s : 8'bz;  // Driver driver_13
  assign regin = dec ? sub_2_s : 8'bz;  // Driver driver_14
  assign calbus = co_add ? add_1_s : 8'bz;  // Driver driver_15
  assign calbus = co_sub ? sub_1_s : 8'bz;  // Driver driver_16
  assign calbus = co_mul ? mul_1_mul[7:0] : 8'bz;  // Driver driver_17
  assign calbus = co_div ? div_1_q : 8'bz;  // Driver driver_18
  assign calbus = co_mod ? div_1_r : 8'bz;  // Driver driver_19
  assign regin = \xor  ? xor_1_out : 8'bz;  // Driver driver_20
  not not_9 (not_9_out, clk);
  Register flag (.D(multiplexer_3_out), .C(not_9_out), .en(1'b1), .Q(flag_out));
  or or_16 (or_16_out, co_add, co_sub);
  and and_23 (and_23_out, co_add, cary_coadd);
  and and_24 (and_24_out, co_sub, cary_cosub);
  and and_25 (and_25_out, ~or_16_out, flag_out);  // And
  assign and_26_out = regout_arg0 & regout_arg1;  // And and_26, 8 bits wide
  assign or_17_out = regout_arg0 | regout_arg1;  // Or or_17, 8 bits wide
  assign not_10_out = ~regout_arg0;  // Not not_10, 8 bits wide
  BarrelShifter #(.Bits(8)) barrelshifter_1 (.in(regout_arg0), .shift(regout_arg1[3:0]), .out(barrelshifter_1_out));
  BarrelShifter #(.Bits(8), .direction("right")) barrelshifter_2 (
    .in(regout_arg0), .shift(regout_arg1[3:0]), .out(barrelshifter_2_out));
  BarrelShifter #(.Bits(8), .barrelShifterMode("rotate")) barrelshifter_3 (
    .in(regout_arg0), .shift(regout_arg1[3:0]), .out(barrelshifter_3_out));
  BarrelShifter #(.Bits(8), .barrelShifterMode("rotate")) barrelshifter_4 (
    .in(regout_arg0), .shift(regout_arg1[3:0]), .out(barrelshifter_4_out));
  or or_18 (cal_flag, and_23_out, and_24_out, and_25_out);
  assign calbus = co_and ? and_26_out : 8'bz;  // Driver driver_21
  assign calbus = co_or ? or_17_out : 8'bz;  // Driver driver_22
  assign calbus = co_not ? not_10_out : 8'bz;  // Driver driver_23
  assign calbus = co_shl ? barrelshifter_1_out : 8'bz;  // Driver driver_24
  assign calbus = co_shr ? barrelshifter_2_out : 8'bz;  // Driver driver_25
  assign calbus = co_ror ? barrelshifter_3_out : 8'bz;  // Driver driver_26
  assign calbus = co_rol ? barrelshifter_4_out : 8'bz;  // Driver driver_27

  // Other names for the same wires on the sheet: arg1[1:0] = arg[1:0]; arg0[1:0] = arg[3:2]; addrbus[7:0] = A[7:0];
  //   addrbus_full[15:0] = A; bankbus[7:0] = A[15:8]; clock = clk; reset = rst

  // Notes on the sheet:
  //   clk: Hz: 2000
  //   A: address bus
  //   D: databus
  //   dread: the processor wants to read the address on the address bus
  //   dwrite: The processor wants to write to the address on the address bus
  //   rst: Reset the processor
  //   operations
  //   op decoder
  //   jmp bra
  //   mov
  //   mwr, mrd
  //   flg
  //   sin
  //   lil lih
  //   IO
  //   memory
  //   registers
  //   for mrd instruction only set reg_we on the xcylce
  //   select r0 on lil,lih ops
  //   pc,clock
  //   alu
  //   inc dec
  //   arithmetic
  //   flag
  //   calbus link
  //   flag ctrl
  //   logical
  //   shifts
endmodule
