// Digital circuit shifter8.dig as structural Verilog
module shifter8 (
  input  [7:0] in,
  input  sbit,
  output [7:0] out,
  output obit
);

  // Pins of 1 and 8 bits meet at {in[6:0], sbit}

  assign obit = in[7];
  assign out = {in[6:0], sbit};

  // Notes on the sheet:
  //   sbit: Bit to be shifted in
  //   obit: Bit that gets shifted out
endmodule
