// Digital circuit video.dig as structural Verilog
module video (
  input  clk,
  input  [15:0] A,
  input  dwrite,
  input  dread,
  output [7:0] D
);

  wire addr_video, addr_vm, and_1_out, and_2_out, and_3_out, and_4_out;
  wire [7:0] vm;

  Comparator #(.Bits(16)) comparator_1 (.a(A), .b(16'hff03), .eq(addr_vm));  // open: gt, lt
  and and_1 (and_1_out, dwrite, addr_vm);
  Comparator #(.Bits(8)) comparator_2 (.a(A[15:8]), .b(8'hfe), .eq(addr_video));  // open: gt, lt
  Register #(.Bits(8)) u_vm (.D(D), .C(clk), .en(and_1_out), .Q(vm));
  and and_2 (and_2_out, dwrite, addr_video);
  and and_3 (and_3_out, dread, addr_video);
  and and_4 (and_4_out, dread, addr_vm);
  assign D = and_4_out ? vm : 8'bz;  // Driver driver_1
  GraphicCard #(.graphicHeight(16), .graphicWidth(16), .Bits(8)) graphiccard_1 (
    .A({1'b0, A[7:0]}), .str(and_2_out), .C(clk), .ld(and_3_out), .B(1'b0), .D(D));

  // Other names for the same wires on the sheet: addrbus[15:0] = A; clock = clk; databus[7:0] = D

  // Notes on the sheet:
  //   vram
  //   vm register
endmodule
